# Fritzing sketch stewart2 (saved by Fritzing 0.9.9b)
circuit board: 14.5196cm x 11.4252cm

parts:
  Part2 = LCD Display 16x2 [part_number=LCD]
  S1 = Round Pushbutton [part_number=R/S]
  S2 = Round Pushbutton [part_number=Time]
  S3 = Round Pushbutton [part_number=Pos]
  Part1 = Arduino Mega 2560 (Rev3)
  LED2 = LED - 5mm [color="Red (633nm)" current=0.030 package="5 mm [THT]"]
  LED3 = LED - 5mm [color="Red (633nm)" current=0.030 package="5 mm [THT]"]
  LED4 = LED - 5mm [color="Red (633nm)" current=0.030 package="5 mm [THT]"]
  R1 = Resistor [tolerance=±5% resistance=220 package="0805 [SMD]"]
  R3 = Resistor [tolerance=±5% resistance=220 package="0805 [SMD]"]
  R4 = Resistor [tolerance=±5% resistance=220 package="0805 [SMD]"]
  JP9 = Header 4 [package=jst-4-pth]
  JP10 = Header 4 [package=jst-4-pth]
  JP11 = Header 4 [package=jst-4-pth]
  JP12 = Header 4 [package=jst-4-pth]
  JP13 = Header 4 [package=jst-4-pth]
  JP14 = Header 4 [package=jst-4-pth]
  JP17 = Header 5 [package=jst-5-pth]
  JP18 = Header 5 [package=jst-5-pth]

nets:
  N1: Part2.aún_sin_nombre#0, Part2.aún_sin_nombre#4, S1.leg1, S2.leg1, S3.leg1, Part1.GND, R1.Pin_0, R3.Pin_0, R4.Pin_0, JP9.1, JP10.1, JP11.1, JP12.1, JP13.1, JP14.1, JP17.4, JP18.4
  N2: Part2.aún_sin_nombre#1, Part1.5V, JP9.2, JP10.2, JP11.2, JP12.2, JP13.2, JP14.2, JP17.5, JP18.5
  N3: Part2.aún_sin_nombre#3, Part1.D14/TX3
  N4: Part2.aún_sin_nombre#5, Part1.D15/RX3
  N5: Part2.aún_sin_nombre#10, Part1.D16_PWM/TX2
  N6: Part2.aún_sin_nombre#11, Part1.D17_PWM/RX2
  N7: Part2.aún_sin_nombre#12, Part1.D18/TX1
  N8: Part2.aún_sin_nombre#13, Part1.D19/RX1
  N9: S1.leg0, Part1.D44
  N10: S2.leg0, Part1.D46
  N11: S3.leg0, Part1.D45
  N12: Part1.A0, JP17.3
  N13: Part1.A1, JP17.2
  N14: Part1.A2, JP17.1
  N15: Part1.A3, JP18.3
  N16: Part1.A4, JP18.2
  N17: Part1.A5, JP18.1
  N18: Part1.D11_PWM, JP10.4
  N19: Part1.D10_PWM, JP9.4
  N20: Part1.D9_PWM, JP14.4
  N21: Part1.D8_PWM, JP13.4
  N22: Part1.D3_PWM, LED2.anode
  N23: Part1.D4_PWM, LED3.anode
  N24: Part1.D5_PWM, LED4.anode
  N25: Part1.D6_PWM, JP11.4
  N26: Part1.D7_PWM, JP12.4
  N27: LED2.cathode, R4.Pin_1
  N28: LED3.cathode, R1.Pin_1
  N29: LED4.cathode, R3.Pin_1

custom parts:
  Header 5: Header 5 Standard 5-pin 2mm header. Rev3
